// Logisim project ALUOp1.circ as structural Verilog: 1 circuit, main circuit ALUOP3
module ALUOP3 (
  input  [4:0] OP,
  input  [1:0] FUNC,
  output [3:0] ALUOp
);

  wire and_1_out, and_2_out, and_3_out, and_4_out, and_5_out, and_6_out, and_7_out, and_8_out, and_9_out,
       not_1_out, not_2_out, not_3_out, not_4_out, not_5_out;

  not not_1 (not_1_out, OP[4]);
  not not_2 (not_2_out, OP[3]);
  not not_3 (not_3_out, OP[2]);
  not not_4 (not_4_out, OP[1]);
  not not_5 (not_5_out, OP[0]);
  and and_1 (and_1_out, not_3_out, OP[0]);
  and and_2 (and_2_out, OP[3], not_3_out, OP[1]);
  and and_3 (and_3_out, not_2_out, not_4_out, not_5_out);
  and and_4 (and_4_out, not_2_out, OP[1], OP[0]);
  and and_5 (and_5_out, not_2_out, FUNC[1]);
  and and_6 (and_6_out, OP[3], not_3_out, OP[1], OP[0]);
  and and_7 (and_7_out, not_2_out, FUNC[0]);
  and and_8 (and_8_out, OP[3], OP[1], not_5_out);
  and and_9 (and_9_out, not_1_out, OP[2], OP[1]);
  or or_1 (ALUOp[3], and_1_out, and_2_out);
  or or_2 (ALUOp[2], and_3_out, and_4_out);
  or or_3 (ALUOp[1], and_5_out, and_6_out);
  or or_4 (ALUOp[0], and_7_out, and_8_out, and_9_out);
endmodule
