// Logisim project Baraa 1.circ as structural Verilog: 1 circuit, main circuit main
module main (
);

  wire and0_1_p3, controlled_buffer_1_out, controlled_buffer_3_out, decoder_1_out0, decoder_1_out1,
       decoder_1_out2, decoder_1_out3, decoder_1_out4, decoder_1_out5, decoder_1_out6, decoder_2_out0,
       decoder_3_out0, register_1_p4, undriven;

  Decoder #(.enable("false"), .select(3)) decoder_1 (
    .out0(decoder_1_out0), .out1(decoder_1_out1), .out2(decoder_1_out2), .out3(decoder_1_out3),
    .out4(decoder_1_out4), .out5(decoder_1_out5), .out6(decoder_1_out6));  // open: out7, sel
  // and0 and0_1: pin names not known; wires that end beside it: decoder_1_out0, decoder_1_out1, and0_1_p3
  Decoder #(.enable("false"), .select(3)) decoder_2 (.out0(decoder_2_out0));  // open: out1, out2, out3, out4, out5, out6, out7, sel
  // Register register_1: pin names not known; wires that end beside it: decoder_1_out0, decoder_1_out1, and0_1_p3, register_1_p4
  assign controlled_buffer_1_out = decoder_2_out0 ? undriven : 1'bz;  // Controlled_Buffer controlled_buffer_1
  Controlled_Buffer controlled_buffer_2 (.in(register_1_p4), .out(controlled_buffer_1_out));  // open: en
  Decoder #(.enable("false"), .select(3)) decoder_3 (.out0(decoder_3_out0));  // open: out1, out2, out3, out4, out5, out6, out7, sel
  Controlled_Buffer controlled_buffer_3 (.in(register_1_p4), .out(controlled_buffer_3_out));  // open: en
  Controlled_Buffer controlled_buffer_4 (.out(controlled_buffer_3_out), .en(decoder_3_out0));  // open: in
endmodule
