// Logisim project Belal_ALU.circ as structural Verilog: 1 circuit, main circuit ALU
module ALU (
  input  [15:0] A,
  input  [15:0] B,
  input  [3:0] ALUOp,
  output ZeroFlag,
  output [15:0] ALUOutput
);

  wire [15:0] arithmeticunit_1_outputar, logicunit_1_outputlogic, reverse_1_outputreverse,
       shiftunit_1_outputshift;

  shiftUnit shiftunit_1 (.A(A), .B(B), .SelectShift(ALUOp[1:0]), .OutputShift(shiftunit_1_outputshift));
  arithmeticUnit arithmeticunit_1 (.A(A), .B(B), .SelectAR(ALUOp[1:0]), .OutputAR(arithmeticunit_1_outputar));
  logicUnit logicunit_1 (.A(A), .B(B), .SelectLogic(ALUOp[1:0]), .OutputLogic(logicunit_1_outputlogic));
  reverse reverse_1 (.A(A), .B(B), .SelectReverse(ALUOp[1:0]), .OutputReverse(reverse_1_outputreverse));
  Multiplexer #(.select(2), .width(16)) multiplexer_1 (
    .in0(shiftunit_1_outputshift), .in1(arithmeticunit_1_outputar), .in2(logicunit_1_outputlogic),
    .in3(reverse_1_outputreverse), .out(ALUOutput), .sel(ALUOp[3:2]));
  Comparator #(.width(16)) comparator_1 (.a({16{1'b0}}), .b(ALUOutput), .eq(ZeroFlag));  // open: gt, lt
endmodule
