// Logisim project Belal_Single_Cycle_CPU.circ as structural Verilog: 6 circuits, main circuit main
module main (
);

  wire clock_1_out, EXTOp, JAL, LUI, MemRead, MemWrite, not_1_out, not_2_out, RegWrite, REVSrc, WBData,
       ZeroFlag;
  wire [1:0] ALUSrc, func, pc_ctrl2_3_1_pcsrc, RegDst;
  wire [2:0] multiplexer_2_out, multiplexer_3_out, splt_1_rd, splt_1_rs, splt_1_rt;
  wire [3:0] aluop3_5_1_aluop;
  wire [4:0] OP, splt_1_imm5;
  wire [10:0] splt_1_imm11;
  wire [15:0] adder_1_out, adder_2_out, alu_1_aluoutput, bit_extender_1_out, bit_extender_2_out,
       multiplexer_1_out, multiplexer_4_out, multiplexer_5_out, multiplexer_6_out, multiplexer_7_out,
       ram_1_dout, register_1_q, registerfile_1_busa, registerfile_1_busb, rom_1_data;

  Multiplexer #(.select(2), .width(16)) multiplexer_1 (
    .in0(adder_1_out), .in1(bit_extender_1_out), .in2(adder_2_out), .in3(registerfile_1_busa),
    .out(multiplexer_1_out), .sel(pc_ctrl2_3_1_pcsrc));
  PC_Ctrl2_3 pc_ctrl2_3_1 (.OP(OP), .FUNC(func), .Zero(ZeroFlag), .PCSrc(pc_ctrl2_3_1_pcsrc));
  Adder #(.width(16)) adder_1 (.a(16'h1), .b(register_1_q), .out(adder_1_out));  // open: cin, cout
  Register #(.width(16)) register_1 (.D(multiplexer_1_out), .Q(register_1_q), .clk(clock_1_out));  // open: en, clr
  Clock clock_1 (.out(clock_1_out));
  ROM #(.addrWidth(16), .dataWidth(16)) rom_1 (.addr(register_1_q), .data(rom_1_data));
  Adder #(.width(16)) adder_2 (.a(register_1_q), .b(bit_extender_2_out), .out(adder_2_out));  // open: cin, cout
  Splt splt_1 (
    .Inst16(rom_1_data), .Imm11(splt_1_imm11), .Op(OP), .Imm5(splt_1_imm5), .Rt(splt_1_rt), .Rs(splt_1_rs),
    .Rd(splt_1_rd), .f2(func));
  CUv2 cuv2_1 (
    .OP(OP), .RegDst(RegDst), .RegWrite(RegWrite), .EXTOp(EXTOp), .ALUSrc(ALUSrc), .MemRead(MemRead),
    .MemWrite(MemWrite), .WBData(WBData), .JAL(JAL), .LUI(LUI));
  Multiplexer #(.select(2), .width(3)) multiplexer_2 (
    .in0(splt_1_rt), .in1(splt_1_rd), .in2(3'b001), .in3(3'b111), .out(multiplexer_2_out), .sel(RegDst));
  Multiplexer #(.width(3)) multiplexer_3 (.in0(splt_1_rt), .in1(splt_1_rd), .out(multiplexer_3_out), .sel(REVSrc));
  assign bit_extender_1_out = {{5{1'b0}}, splt_1_imm11};  // Bit_Extender bit_extender_1
  assign bit_extender_2_out = {{11{splt_1_imm5[4]}}, splt_1_imm5};  // Bit_Extender bit_extender_2
  registerFile registerfile_1 (
    .RW(multiplexer_2_out), .RegW(RegWrite), .BusW(multiplexer_4_out), .RA(splt_1_rs),
    .RB(multiplexer_3_out), .BusA(registerfile_1_busa), .BusB(registerfile_1_busb));
  Multiplexer #(.width(16)) multiplexer_4 (
    .in0(adder_1_out), .in1(multiplexer_7_out), .out(multiplexer_4_out), .sel(not_1_out));
  not not_1 (not_1_out, JAL);
  not not_2 (not_2_out, LUI);
  Multiplexer #(.width(16)) multiplexer_5 (
    .in0(bit_extender_1_out), .in1(registerfile_1_busa), .out(multiplexer_5_out), .sel(not_2_out));
  Multiplexer #(.select(2), .width(16)) multiplexer_6 (
    .in0(registerfile_1_busb), .in1(bit_extender_2_out), .in2(16'h5), .out(multiplexer_6_out), .sel(ALUSrc));  // open: in3
  ALU alu_1 (
    .ALUOp(aluop3_5_1_aluop), .A(multiplexer_5_out), .B(multiplexer_6_out), .ALUOutput(alu_1_aluoutput),
    .ZeroFlag(ZeroFlag));
  ALUOP3_5 aluop3_5_1 (.OP(OP), .FUNC(func), .ALUOp(aluop3_5_1_aluop));
  REVSrc revsrc_1 (.OP(OP), .func(func), .REV_Src(REVSrc));
  RAM #(.addrWidth(16), .asyncread("true"), .dataWidth(16)) ram_1 (
    .addr(alu_1_aluoutput), .we(MemWrite), .oe(MemRead), .clk(clock_1_out), .din(registerfile_1_busb),
    .dout(ram_1_dout));
  Multiplexer #(.width(16)) multiplexer_7 (
    .in0(alu_1_aluoutput), .in1(ram_1_dout), .out(multiplexer_7_out), .sel(WBData));

  // Notes on the sheet:
  //   contents of rom_1 (hex, n*v repeats v):
  //   4141 a88 51c3 d1a 95c f84 495f 4a 28b 4f2 732 5955 104a 12f2 1532 175a ff6c 1c88 1a50 1888 4182 6914
  //   6115 68d5 168 cc9 7918 47db 70eb 4001 7959 77a5 0 0 0 8030 7009 11*0 4283 4004 40c5 6815 4064 4052
  //   7f63 4001 883a 8024 0 c92 4243 4006 680e 4049 4076 680e 67cc 600d 1ac 4049 4052 7e93 1e38
endmodule

module registerFile (
  input  [2:0] RA,
  input  [2:0] RB,
  input  [15:0] BusW,
  input  [2:0] RW,
  input  RegW,
  output [15:0] BusB,
  output [15:0] BusA
);

  wire and_1_out, and_2_out, and_3_out, and_4_out, and_5_out, and_6_out, and_7_out, clock_1_out,
       decoder_1_out1, decoder_1_out2, decoder_1_out3, decoder_1_out4, decoder_1_out5, decoder_1_out6,
       decoder_1_out7, decoder_2_out0, decoder_2_out1, decoder_2_out2, decoder_2_out3, decoder_2_out4,
       decoder_2_out5, decoder_2_out6, decoder_2_out7, decoder_3_out0, decoder_3_out1, decoder_3_out2,
       decoder_3_out3, decoder_3_out4, decoder_3_out5, decoder_3_out6, decoder_3_out7;
  wire [15:0] register_1_q, register_2_q, register_3_q, register_4_q, register_5_q, register_6_q,
       register_7_q;

  Decoder #(.enable("false"), .select(3)) decoder_1 (
    .out1(decoder_1_out1), .out2(decoder_1_out2), .out3(decoder_1_out3), .out4(decoder_1_out4),
    .out5(decoder_1_out5), .out6(decoder_1_out6), .out7(decoder_1_out7), .sel(RW));  // open: out0
  and and_1 (and_1_out, decoder_1_out1, RegW);
  and and_2 (and_2_out, decoder_1_out2, RegW);
  and and_3 (and_3_out, decoder_1_out3, RegW);
  and and_4 (and_4_out, decoder_1_out4, RegW);
  and and_5 (and_5_out, decoder_1_out5, RegW);
  and and_6 (and_6_out, decoder_1_out6, RegW);
  and and_7 (and_7_out, decoder_1_out7, RegW);
  Decoder #(.enable("false"), .select(3)) decoder_2 (
    .out0(decoder_2_out0), .out1(decoder_2_out1), .out2(decoder_2_out2), .out3(decoder_2_out3),
    .out4(decoder_2_out4), .out5(decoder_2_out5), .out6(decoder_2_out6), .out7(decoder_2_out7), .sel(RA));
  Register #(.width(16)) register_1 (.D(BusW), .en(and_1_out), .Q(register_1_q), .clk(clock_1_out));  // open: clr
  Register #(.width(16)) register_2 (.D(BusW), .en(and_2_out), .Q(register_2_q), .clk(clock_1_out));  // open: clr
  Register #(.width(16)) register_3 (.D(BusW), .en(and_3_out), .Q(register_3_q), .clk(clock_1_out));  // open: clr
  Register #(.width(16)) register_4 (.D(BusW), .en(and_4_out), .Q(register_4_q), .clk(clock_1_out));  // open: clr
  Register #(.width(16)) register_5 (.D(BusW), .en(and_5_out), .Q(register_5_q), .clk(clock_1_out));  // open: clr
  Register #(.width(16)) register_6 (.D(BusW), .en(and_6_out), .Q(register_6_q), .clk(clock_1_out));  // open: clr
  Register #(.width(16)) register_7 (.D(BusW), .en(and_7_out), .Q(register_7_q), .clk(clock_1_out));  // open: clr
  Clock clock_1 (.out(clock_1_out));
  assign BusA = decoder_2_out0 ? {16{1'b0}} : 16'bz;  // Controlled_Buffer controlled_buffer_1
  assign BusA = decoder_2_out1 ? register_1_q : 16'bz;  // Controlled_Buffer controlled_buffer_2
  assign BusA = decoder_2_out2 ? register_2_q : 16'bz;  // Controlled_Buffer controlled_buffer_3
  assign BusA = decoder_2_out3 ? register_3_q : 16'bz;  // Controlled_Buffer controlled_buffer_4
  assign BusA = decoder_2_out4 ? register_4_q : 16'bz;  // Controlled_Buffer controlled_buffer_5
  assign BusA = decoder_2_out5 ? register_5_q : 16'bz;  // Controlled_Buffer controlled_buffer_6
  assign BusA = decoder_2_out6 ? register_6_q : 16'bz;  // Controlled_Buffer controlled_buffer_7
  assign BusA = decoder_2_out7 ? register_7_q : 16'bz;  // Controlled_Buffer controlled_buffer_8
  Decoder #(.enable("false"), .select(3)) decoder_3 (
    .out0(decoder_3_out0), .out1(decoder_3_out1), .out2(decoder_3_out2), .out3(decoder_3_out3),
    .out4(decoder_3_out4), .out5(decoder_3_out5), .out6(decoder_3_out6), .out7(decoder_3_out7), .sel(RB));
  assign BusB = decoder_3_out1 ? register_1_q : 16'bz;  // Controlled_Buffer controlled_buffer_9
  assign BusB = decoder_3_out2 ? register_2_q : 16'bz;  // Controlled_Buffer controlled_buffer_10
  assign BusB = decoder_3_out3 ? register_3_q : 16'bz;  // Controlled_Buffer controlled_buffer_11
  assign BusB = decoder_3_out4 ? register_4_q : 16'bz;  // Controlled_Buffer controlled_buffer_12
  assign BusB = decoder_3_out5 ? register_5_q : 16'bz;  // Controlled_Buffer controlled_buffer_13
  assign BusB = decoder_3_out6 ? register_6_q : 16'bz;  // Controlled_Buffer controlled_buffer_14
  assign BusB = decoder_3_out7 ? register_7_q : 16'bz;  // Controlled_Buffer controlled_buffer_15
  assign BusB = decoder_3_out0 ? {16{1'b0}} : 16'bz;  // Controlled_Buffer controlled_buffer_16
endmodule

module PC_Ctrl2_2 (
  input  [4:0] OP,
  input  [1:0] FUNC,
  input  Zero,
  output [1:0] PCSrc
);

  wire not_1_out, not_2_out, not_3_out, not_4_out;

  not not_1 (not_1_out, OP[4]);
  not not_2 (not_2_out, OP[3]);
  not not_3 (not_3_out, OP[2]);
  not not_4 (not_4_out, OP[1]);
  and and_1 (PCSrc[1], not_1_out, OP[3], OP[2], OP[1], Zero);
  and and_2 (PCSrc[0], OP[4], not_2_out, not_3_out, not_4_out);
endmodule

module REVSrc (
  input  [4:0] OP,
  input  [1:0] func,
  output REV_Src
);

  wire not_1_out, not_2_out, not_3_out, not_4_out;

  not not_1 (not_1_out, OP[4]);
  not not_2 (not_2_out, OP[3]);
  not not_3 (not_3_out, OP[2]);
  not not_4 (not_4_out, func[1]);
  and and_1 (REV_Src, not_1_out, not_2_out, not_3_out, OP[1], OP[0], not_4_out);
endmodule

module PC_Ctrl2_3 (
  input  [4:0] OP,
  input  [1:0] FUNC,
  input  Zero,
  output [1:0] PCSrc
);

  wire and_1_out, and_2_out, not_1_out, not_2_out, not_3_out, not_4_out, not_5_out, not_6_out;

  not not_1 (not_1_out, OP[4]);
  not not_2 (not_2_out, OP[3]);
  not not_3 (not_3_out, OP[2]);
  not not_4 (not_4_out, OP[1]);
  not not_5 (not_5_out, OP[0]);
  not not_6 (not_6_out, Zero);
  and and_1 (and_1_out, not_1_out, OP[3], OP[2], OP[1], not_5_out, Zero);
  and and_2 (and_2_out, not_1_out, OP[3], OP[2], OP[1], OP[0], not_6_out);
  and and_3 (PCSrc[0], OP[4], not_2_out, not_3_out, not_4_out);
  or or_1 (PCSrc[1], and_1_out, and_2_out);
endmodule

module ALUOP3_5 (
  input  [4:0] OP,
  input  [1:0] FUNC,
  output [3:0] ALUOp
);

  wire and_1_out, and_2_out, and_3_out, and_4_out, and_5_out, and_6_out, and_7_out, and_8_out, and_9_out,
       and_10_out, and_11_out, not_1_out, not_2_out, not_3_out, not_4_out, not_5_out;

  not not_1 (not_1_out, OP[4]);
  not not_2 (not_2_out, OP[3]);
  not not_3 (not_3_out, OP[2]);
  not not_4 (not_4_out, OP[1]);
  not not_5 (not_5_out, OP[0]);
  and and_1 (and_1_out, not_3_out, OP[0]);
  and and_2 (and_2_out, OP[3], not_3_out, OP[1]);
  and and_3 (and_3_out, not_2_out, OP[1], OP[0]);
  and and_4 (and_4_out, not_1_out, not_4_out, not_5_out);
  and and_5 (and_5_out, not_1_out, OP[3], OP[2]);
  and and_6 (and_6_out, not_2_out, not_4_out, not_5_out);
  and and_7 (and_7_out, not_2_out, FUNC[1]);
  and and_8 (and_8_out, OP[3], not_3_out, OP[1], OP[0]);
  and and_9 (and_9_out, not_2_out, FUNC[0]);
  and and_10 (and_10_out, OP[3], OP[1], not_5_out);
  and and_11 (and_11_out, not_1_out, OP[2], OP[1]);
  or or_1 (ALUOp[3], and_1_out, and_2_out);
  or or_2 (ALUOp[2], and_3_out, and_4_out, and_5_out, and_6_out);
  or or_3 (ALUOp[1], and_7_out, and_8_out);
  or or_4 (ALUOp[0], and_9_out, and_10_out, and_11_out);
endmodule
