// Logisim project CU.circ as structural Verilog: 1 circuit, main circuit CUv2
module CUv2 (
  input  [4:0] OP,
  output [1:0] RegDst,
  output RegWrite,
  output EXTOp,
  output [1:0] ALUSrc,
  output MemRead,
  output MemWrite,
  output WBData,
  output JAL,
  output LUI
);

  wire and_1_out, and_2_out, and_3_out, and_4_out, and_5_out, and_6_out, not_1_out, not_3_out, not_4_out,
       not_5_out;

  not not_1 (not_1_out, OP[4]);
  not not_2 (RegDst[0], OP[3]);
  not not_3 (not_3_out, OP[2]);
  not not_4 (not_4_out, OP[1]);
  not not_5 (not_5_out, OP[0]);
  and and_1 (and_1_out, not_1_out, not_3_out);
  and and_2 (and_2_out, not_1_out, not_4_out, not_5_out);
  and and_3 (and_3_out, OP[4], OP[0]);
  and and_4 (and_4_out, not_4_out, not_5_out);
  and and_5 (and_5_out, OP[3], not_3_out);
  and and_6 (and_6_out, OP[2], not_4_out);
  and and_7 (MemRead, OP[2], not_4_out, not_5_out);
  and and_8 (MemWrite, OP[2], not_4_out, OP[0]);
  and and_9 (WBData, OP[2], not_4_out);
  and and_10 (JAL, OP[4], RegDst[0], OP[0]);
  and and_11 (LUI, OP[4], OP[1]);
  or or_1 (RegWrite, and_1_out, and_2_out, and_3_out);
  or or_2 (EXTOp, and_4_out, OP[2]);
  or or_3 (ALUSrc[0], and_5_out, and_6_out);

  assign ALUSrc[1] = OP[4];
  assign RegDst[1] = OP[4];
endmodule
