// Logisim project DataMemory.circ as structural Verilog: 1 circuit, main circuit dataMemory
module dataMemory (
);

  wire clock_1_out, undriven_2, undriven_3;
  wire [15:0] ram_1_dout, undriven, undriven_4;

  Clock clock_1 (.out(clock_1_out));
  RAM #(.addrWidth(16), .dataWidth(16)) ram_1 (
    .addr(undriven), .we(undriven_2), .oe(undriven_3), .clk(clock_1_out), .din(undriven_4), .dout(ram_1_dout));
endmodule
