// Logisim project PIPELINED CPU.circ as structural Verilog: 17 circuits, main circuit pip
module pip (
);

  wire and_1_out, BEQ, BNE, clock_1_out, cu_pipe4_1_beq, cu_pipe4_1_bne, cu_pipe4_1_jal, cu_pipe4_1_lui,
       cu_pipe4_1_memread, cu_pipe4_1_memwrite, cu_pipe4_1_regwrite, cu_pipe4_1_wbdata, ex_1_jal, ex_1_memrd,
       ex_1_memwr, ex_1_regw, ex_1_wbdata, EXTOp, hazard_detect_and_forward_1_stall, J, JAL, Jr, Kill1,
       Kill2, LUI, mem_1_jal, mem_1_regw, MemRead, MemWrite, not_1_out, not_2_out, not_3_out, or_1_out,
       RegWrite, REV_Src1, stallmux_1_beq_out, stallmux_1_bne_out, stallmux_1_jal_out, stallmux_1_lui_out,
       stallmux_1_memread_out, stallmux_1_memwrite_out, stallmux_1_regwrite_out, stallmux_1_wbdata_out,
       WBData, ZeroFlag;
  wire [1:0] ALUSrc, cu_pipe4_1_alusrc, func, hazard_detect_and_forward_1_forwarda,
       hazard_detect_and_forward_1_forwardb, pc_ctrl_jr_1_pcsrc, RegDst, stallmux_1_alusrc_out;
  wire [2:0] multiplexer_4_out, multiplexer_5_out, Rd2_q, Rd3_q, Rw, splt_1_rd, splt_1_rs, splt_1_rt;
  wire [3:0] ALUOp_1, ALUOp_in, stallmux_1_aluop_out;
  wire [4:0] OP, splt_1_imm5;
  wire [10:0] splt_1_imm11;
  wire [15:0] A_q, adder_1_out, adder_2_out, alu_1_aluoutput, B_q, bit_extender_1_out, bit_extender_2_out,
       BTA_q, D_q, Data_q, Imm5_q, Imm11_q, Inst_q, Jal1_q, Jal2_q, Jal3_q, multiplexer_1_out,
       multiplexer_2_out, multiplexer_3_out, multiplexer_6_out, multiplexer_7_out, multiplexer_8_out,
       multiplexer_9_out, multiplexer_10_out, multiplexer_11_out, NextPC, PC_q, R_q, ram_1_dout,
       register_1_q, registerfilee_1_busa, registerfilee_1_busb, rom_1_data;

  Clock clock_1 (.out(clock_1_out));
  Multiplexer #(.select(2), .width(16)) multiplexer_1 (
    .in0(adder_1_out), .in1(adder_1_out), .in2(adder_1_out), .in3(multiplexer_7_out),
    .out(multiplexer_1_out), .sel(func));
  PC_ctrl_jr pc_ctrl_jr_1 (
    .Jr(Jr), .J(J), .BNE(BNE), .BEQ(BEQ), .Zero(ZeroFlag), .PCSrc(pc_ctrl_jr_1_pcsrc), .Kill1(Kill1),
    .Kill2(Kill2));
  Multiplexer #(.select(2), .width(16)) multiplexer_2 (
    .in0(adder_1_out), .in1(bit_extender_1_out), .in2(BTA_q), .in3(multiplexer_1_out),
    .out(multiplexer_2_out), .sel(pc_ctrl_jr_1_pcsrc));
  Register #(.width(16)) register_1 (
    .D(multiplexer_2_out), .en(not_1_out), .Q(register_1_q), .clk(clock_1_out));  // open: clr
  Adder #(.width(16)) adder_1 (.a(16'h1), .b(register_1_q), .out(adder_1_out));  // open: cin, cout
  ROM #(.addrWidth(16), .dataWidth(16)) rom_1 (.addr(register_1_q), .data(rom_1_data));
  Multiplexer #(.width(16)) multiplexer_3 (
    .in0(rom_1_data), .in1({16{1'b0}}), .out(multiplexer_3_out), .sel(and_1_out));
  and and_1 (and_1_out, ~REV_Src1, Kill1);  // AND_Gate
  not not_1 (not_1_out, hazard_detect_and_forward_1_stall);
  Register #(.width(16)) PC (.D(register_1_q), .Q(PC_q), .clk(clock_1_out));  // open: en, clr
  Splt splt_1 (
    .Inst16(Inst_q), .Imm11(splt_1_imm11), .Op(OP), .Imm5(splt_1_imm5), .Rt(splt_1_rt), .Rs(splt_1_rs),
    .Rd(splt_1_rd), .f2(func));
  Register #(.width(16)) Inst (.D(multiplexer_3_out), .en(not_1_out), .Q(Inst_q), .clk(clock_1_out));  // open: clr
  Register #(.width(16)) Jal1 (.D(adder_1_out), .Q(Jal1_q), .clk(clock_1_out));  // open: en, clr
  Multiplexer #(.width(3)) multiplexer_4 (.in0(splt_1_rt), .in1(splt_1_rd), .out(multiplexer_4_out), .sel(REV_Src1));
  Multiplexer #(.select(2), .width(3)) multiplexer_5 (
    .in0(splt_1_rt), .in1(splt_1_rd), .in2(3'b001), .in3(3'b111), .out(multiplexer_5_out), .sel(RegDst));
  CU_Pipe4 cu_pipe4_1 (
    .OP(OP), .RegDst(RegDst), .EXTOp(EXTOp), .RegWrite(cu_pipe4_1_regwrite), .MemRead(cu_pipe4_1_memread),
    .MemWrite(cu_pipe4_1_memwrite), .WBData(cu_pipe4_1_wbdata), .JAL(cu_pipe4_1_jal), .LUI(cu_pipe4_1_lui),
    .ALUSrc(cu_pipe4_1_alusrc), .BEQ(cu_pipe4_1_beq), .BNE(cu_pipe4_1_bne), .J(J), .Jr(Jr));
  ALUCtrl aluctrl_1 (.OP(OP), .FUNC(func), .ALUOp(ALUOp_in));
  RevCtrl2 revctrl2_1 (.OP(OP), .func(func), .x(REV_Src1));
  Adder #(.width(16)) adder_2 (.a(PC_q), .b(bit_extender_2_out), .out(adder_2_out));  // open: cin, cout
  assign bit_extender_1_out = {{5{1'b0}}, splt_1_imm11};  // Bit_Extender bit_extender_1
  assign bit_extender_2_out = {{11{splt_1_imm5[4]}}, splt_1_imm5};  // Bit_Extender bit_extender_2
  registerFilee registerfilee_1 (
    .RW(Rw), .RegW(RegWrite), .BusW(multiplexer_6_out), .RA(splt_1_rs), .clk(clock_1_out),
    .RB(multiplexer_4_out), .BusA(registerfilee_1_busa), .BusB(registerfilee_1_busb));
  Multiplexer #(.width(16)) multiplexer_6 (.in0(NextPC), .in1(Data_q), .out(multiplexer_6_out), .sel(not_2_out));
  not not_2 (not_2_out, JAL);
  Multiplexer #(.select(2), .width(16)) multiplexer_7 (
    .in0(registerfilee_1_busa), .in1(alu_1_aluoutput), .in2(multiplexer_11_out), .in3(Data_q),
    .out(multiplexer_7_out), .sel(hazard_detect_and_forward_1_forwarda));
  Multiplexer #(.select(2), .width(16)) multiplexer_8 (
    .in0(registerfilee_1_busb), .in1(alu_1_aluoutput), .in2(multiplexer_11_out), .in3(Data_q),
    .out(multiplexer_8_out), .sel(hazard_detect_and_forward_1_forwardb));
  Hazard_Detect_And_Forward hazard_detect_and_forward_1 (
    .EX_MemRd(ex_1_memrd), .Ex_RegWr(ex_1_regw), .Mem_RegWr(mem_1_regw), .WB_RegWr(RegWrite), .Rs(splt_1_rs),
    .Rd2(Rd2_q), .Rd3(Rd3_q), .Rd4(Rw), .Rt(multiplexer_4_out),
    .ForwardA(hazard_detect_and_forward_1_forwarda), .ForwardB(hazard_detect_and_forward_1_forwardb),
    .Stall(hazard_detect_and_forward_1_stall));
  or or_1 (or_1_out, hazard_detect_and_forward_1_stall, Kill2);
  StallMUX stallmux_1 (
    .MemRead(cu_pipe4_1_memread), .WBData(cu_pipe4_1_wbdata), .LUI(cu_pipe4_1_lui), .BEQ(cu_pipe4_1_beq),
    .ALUOp(ALUOp_in), .RegWrite(cu_pipe4_1_regwrite), .MemWrite(cu_pipe4_1_memwrite), .JAL(cu_pipe4_1_jal),
    .ALUSrc(cu_pipe4_1_alusrc), .BNE(cu_pipe4_1_bne), .Stall(or_1_out),
    .RegWrite_out(stallmux_1_regwrite_out), .MemWrite_out(stallmux_1_memwrite_out),
    .JAL_out(stallmux_1_jal_out), .ALUSrc_out(stallmux_1_alusrc_out), .BNE_out(stallmux_1_bne_out),
    .MemRead_out(stallmux_1_memread_out), .WBData_out(stallmux_1_wbdata_out), .LUI_out(stallmux_1_lui_out),
    .BEQ_out(stallmux_1_beq_out), .ALUOp_out(stallmux_1_aluop_out));
  Register #(.width(16)) BTA (.D(adder_2_out), .Q(BTA_q), .clk(clock_1_out));  // open: en, clr
  Register #(.width(16)) Imm11 (.D(bit_extender_1_out), .Q(Imm11_q), .clk(clock_1_out));  // open: en, clr
  Register #(.width(16)) Imm5 (.D(bit_extender_2_out), .Q(Imm5_q), .clk(clock_1_out));  // open: en, clr
  Register #(.width(16)) A (.D(multiplexer_7_out), .Q(A_q), .clk(clock_1_out));  // open: en, clr
  Register #(.width(16)) B (.D(multiplexer_8_out), .Q(B_q), .clk(clock_1_out));  // open: en, clr
  Register #(.width(3)) Rd2 (.D(multiplexer_5_out), .Q(Rd2_q), .clk(clock_1_out));  // open: en, clr
  Register #(.width(16)) Jal2 (.D(Jal1_q), .Q(Jal2_q), .clk(clock_1_out));  // open: en, clr
  EX ex_1 (
    .RegW_in(stallmux_1_regwrite_out), .ALUSrc_in(stallmux_1_alusrc_out), .MemRd_in(stallmux_1_memread_out),
    .MemWr_in(stallmux_1_memwrite_out), .WBData_in(stallmux_1_wbdata_out), .JAL_in(stallmux_1_jal_out),
    .LUI_in(stallmux_1_lui_out), .ALUOp_in(stallmux_1_aluop_out), .BEQ_in(stallmux_1_beq_out),
    .BNE_in(stallmux_1_bne_out), .clk(clock_1_out), .RegW(ex_1_regw), .ALUSrc(ALUSrc), .MemRd(ex_1_memrd),
    .MemWr(ex_1_memwr), .WBData(ex_1_wbdata), .JAL(ex_1_jal), .LUI(LUI), .ALUOp(ALUOp_1), .BEQ(BEQ), .BNE(BNE));
  Multiplexer #(.width(16)) multiplexer_9 (.in0(Imm11_q), .in1(A_q), .out(multiplexer_9_out), .sel(not_3_out));
  Multiplexer #(.select(2), .width(16)) multiplexer_10 (
    .in0(B_q), .in1(Imm5_q), .in2(16'h5), .out(multiplexer_10_out), .sel(ALUSrc));  // open: in3
  not not_3 (not_3_out, LUI);
  ALU alu_1 (
    .ALUOp(ALUOp_1), .A(multiplexer_9_out), .B(multiplexer_10_out), .ALUOutput(alu_1_aluoutput),
    .ZeroFlag(ZeroFlag));
  Register #(.width(16)) R (.D(alu_1_aluoutput), .Q(R_q), .clk(clock_1_out));  // open: en, clr
  Register #(.width(16)) D (.D(B_q), .Q(D_q), .clk(clock_1_out));  // open: en, clr
  Register #(.width(3)) Rd3 (.D(Rd2_q), .Q(Rd3_q), .clk(clock_1_out));  // open: en, clr
  Register #(.width(16)) Jal3 (.D(Jal2_q), .Q(Jal3_q), .clk(clock_1_out));  // open: en, clr
  MEM mem_1 (
    .RegW_in(ex_1_regw), .clk(clock_1_out), .MemRd_in(ex_1_memrd), .MemWr_in(ex_1_memwr),
    .WBData_in(ex_1_wbdata), .JAL_in(ex_1_jal), .RegW(mem_1_regw), .MemRd(MemRead), .MemWr(MemWrite),
    .WBData(WBData), .JAL(mem_1_jal));  // open: LUI_in, LUI
  RAM #(.addrWidth(16), .asyncread("true"), .dataWidth(16)) ram_1 (
    .addr(R_q), .we(MemWrite), .oe(MemRead), .clk(clock_1_out), .din(D_q), .dout(ram_1_dout));
  Multiplexer #(.width(16)) multiplexer_11 (.in0(R_q), .in1(ram_1_dout), .out(multiplexer_11_out), .sel(WBData));
  Register #(.width(16)) Data (.D(multiplexer_11_out), .Q(Data_q), .clk(clock_1_out));  // open: en, clr
  Register #(.width(3)) Rd4 (.D(Rd3_q), .Q(Rw), .clk(clock_1_out));  // open: en, clr
  Register #(.width(16)) Jal4 (.D(Jal3_q), .Q(NextPC), .clk(clock_1_out));  // open: en, clr
  WB wb_1 (
    .RegW_in(mem_1_regw), .JAL_in(mem_1_jal), .clk(clock_1_out), .RegW(RegWrite), .JAL(JAL));  // open: LUI_in, LUI

  // Notes on the sheet:
  //   contents of rom_1 (hex, n*v repeats v):
  //   4141 a88 51c3 d1a 95c f84 495f 4a 28b 4f2 732 5955 104a 12f2 1532 175a ff6c 1c88 1a50 1888 4182 6914
  //   6115 68d5 168 cc9 7918 47db 70eb 4001 7959 77a5 0 0 0 8030 7009 11*0 4283 4004 40c5 6815 4064 4052
  //   7f63 4001 883a 8024 0 c92 4243 4006 680e 4049 4076 680e 67cc 600d 1ac 4049 4052 7e93 1e38
endmodule

module RevCtrl (
  input  [4:0] OP,
  input  [1:0] func,
  output out_3
);

  wire not_1_out, not_2_out, not_3_out, not_4_out;

  not not_1 (not_1_out, OP[4]);
  not not_2 (not_2_out, OP[3]);
  not not_3 (not_3_out, OP[2]);
  not not_4 (not_4_out, func[1]);
  and and_1 (out_3, not_1_out, not_2_out, not_3_out, OP[1], OP[0], not_4_out);
endmodule

module ALUCtrl (
  input  [4:0] OP,
  input  [1:0] FUNC,
  output [3:0] ALUOp
);

  wire and_1_out, and_2_out, and_3_out, and_4_out, and_5_out, and_6_out, and_7_out, and_8_out, and_9_out,
       and_10_out, and_11_out, not_1_out, not_2_out, not_3_out, not_4_out, not_5_out;

  not not_1 (not_1_out, OP[4]);
  not not_2 (not_2_out, OP[3]);
  not not_3 (not_3_out, OP[2]);
  not not_4 (not_4_out, OP[1]);
  not not_5 (not_5_out, OP[0]);
  and and_1 (and_1_out, not_3_out, OP[0]);
  and and_2 (and_2_out, OP[3], not_3_out, OP[1]);
  and and_3 (and_3_out, not_2_out, OP[1], OP[0]);
  and and_4 (and_4_out, not_1_out, not_4_out, not_5_out);
  and and_5 (and_5_out, not_1_out, OP[3], OP[2]);
  and and_6 (and_6_out, not_2_out, not_4_out, not_5_out);
  and and_7 (and_7_out, not_2_out, FUNC[1]);
  and and_8 (and_8_out, OP[3], not_3_out, OP[1], OP[0]);
  and and_9 (and_9_out, not_2_out, FUNC[0]);
  and and_10 (and_10_out, OP[3], OP[1], not_5_out);
  and and_11 (and_11_out, not_1_out, OP[2], OP[1]);
  or or_1 (ALUOp[3], and_1_out, and_2_out);
  or or_2 (ALUOp[2], and_3_out, and_4_out, and_5_out, and_6_out);
  or or_3 (ALUOp[1], and_7_out, and_8_out);
  or or_4 (ALUOp[0], and_9_out, and_10_out, and_11_out);
endmodule

module CU (
  input  [4:0] OP,
  output [1:0] RegDst,
  output RegWrite,
  output EXTOp,
  output [1:0] ALUSrc,
  output MemRead,
  output MemWrite,
  output WBData,
  output JAL,
  output LUI
);

  wire and_1_out, and_2_out, and_3_out, and_4_out, and_5_out, and_6_out, not_1_out, not_3_out, not_4_out,
       not_5_out;

  not not_1 (not_1_out, OP[4]);
  not not_2 (RegDst[0], OP[3]);
  not not_3 (not_3_out, OP[2]);
  not not_4 (not_4_out, OP[1]);
  not not_5 (not_5_out, OP[0]);
  and and_1 (and_1_out, not_1_out, not_3_out);
  and and_2 (and_2_out, not_1_out, not_4_out, not_5_out);
  and and_3 (and_3_out, OP[4], OP[0]);
  and and_4 (and_4_out, not_4_out, not_5_out);
  and and_5 (and_5_out, OP[3], not_3_out);
  and and_6 (and_6_out, OP[2], not_4_out);
  and and_7 (MemRead, OP[2], not_4_out, not_5_out);
  and and_8 (MemWrite, OP[2], not_4_out, OP[0]);
  and and_9 (WBData, OP[2], not_4_out);
  and and_10 (JAL, OP[4], RegDst[0], OP[0]);
  and and_11 (LUI, OP[4], OP[1]);
  or or_1 (RegWrite, and_1_out, and_2_out, and_3_out);
  or or_2 (EXTOp, and_4_out, OP[2]);
  or or_3 (ALUSrc[0], and_5_out, and_6_out);

  assign ALUSrc[1] = OP[4];
  assign RegDst[1] = OP[4];
endmodule

module Split (
  input  [15:0] Inst16,
  output [10:0] Imm11,
  output [4:0] Op,
  output [2:0] Rt,
  output [2:0] Rs,
  output [4:0] Imm5,
  output [2:0] Rd,
  output [1:0] f2
);


  assign f2 = Inst16[10:9];
  assign Imm5 = Inst16[10:6];
  assign Imm11 = Inst16[10:0];
  assign Op = Inst16[15:11];
  assign Rd = Inst16[8:6];
  assign Rs = Inst16[5:3];
  assign Rt = Inst16[2:0];
endmodule

module registerFilee (
  input  [2:0] RA,
  input  [2:0] RB,
  input  [15:0] BusW,
  input  [2:0] RW,
  input  clk,
  input  RegW,
  output [15:0] BusB,
  output [15:0] BusA
);

  wire and_1_out, and_2_out, and_3_out, and_4_out, and_5_out, and_6_out, and_7_out, decoder_1_out1,
       decoder_1_out2, decoder_1_out3, decoder_1_out4, decoder_1_out5, decoder_1_out6, decoder_1_out7,
       decoder_2_out0, decoder_2_out1, decoder_2_out2, decoder_2_out3, decoder_2_out4, decoder_2_out5,
       decoder_2_out6, decoder_2_out7, decoder_3_out0, decoder_3_out1, decoder_3_out2, decoder_3_out3,
       decoder_3_out4, decoder_3_out5, decoder_3_out6, decoder_3_out7;
  wire [15:0] register_1_q, register_2_q, register_3_q, register_4_q, register_5_q, register_6_q,
       register_7_q;

  Decoder #(.enable("false"), .select(3)) decoder_1 (
    .out1(decoder_1_out1), .out2(decoder_1_out2), .out3(decoder_1_out3), .out4(decoder_1_out4),
    .out5(decoder_1_out5), .out6(decoder_1_out6), .out7(decoder_1_out7), .sel(RW));  // open: out0
  and and_1 (and_1_out, decoder_1_out1, RegW);
  and and_2 (and_2_out, decoder_1_out2, RegW);
  and and_3 (and_3_out, decoder_1_out3, RegW);
  and and_4 (and_4_out, decoder_1_out4, RegW);
  and and_5 (and_5_out, decoder_1_out5, RegW);
  and and_6 (and_6_out, decoder_1_out6, RegW);
  and and_7 (and_7_out, decoder_1_out7, RegW);
  Decoder #(.enable("false"), .select(3)) decoder_2 (
    .out0(decoder_2_out0), .out1(decoder_2_out1), .out2(decoder_2_out2), .out3(decoder_2_out3),
    .out4(decoder_2_out4), .out5(decoder_2_out5), .out6(decoder_2_out6), .out7(decoder_2_out7), .sel(RA));
  Register #(.width(16)) register_1 (.D(BusW), .en(and_1_out), .Q(register_1_q), .clk(clk));  // open: clr
  Register #(.width(16)) register_2 (.D(BusW), .en(and_2_out), .Q(register_2_q), .clk(clk));  // open: clr
  Register #(.width(16)) register_3 (.D(BusW), .en(and_3_out), .Q(register_3_q), .clk(clk));  // open: clr
  Register #(.width(16)) register_4 (.D(BusW), .en(and_4_out), .Q(register_4_q), .clk(clk));  // open: clr
  Register #(.width(16)) register_5 (.D(BusW), .en(and_5_out), .Q(register_5_q), .clk(clk));  // open: clr
  Register #(.width(16)) register_6 (.D(BusW), .en(and_6_out), .Q(register_6_q), .clk(clk));  // open: clr
  Register #(.width(16)) register_7 (.D(BusW), .en(and_7_out), .Q(register_7_q), .clk(clk));  // open: clr
  assign BusA = decoder_2_out0 ? {16{1'b0}} : 16'bz;  // Controlled_Buffer controlled_buffer_1
  assign BusA = decoder_2_out1 ? register_1_q : 16'bz;  // Controlled_Buffer controlled_buffer_2
  assign BusA = decoder_2_out2 ? register_2_q : 16'bz;  // Controlled_Buffer controlled_buffer_3
  assign BusA = decoder_2_out3 ? register_3_q : 16'bz;  // Controlled_Buffer controlled_buffer_4
  assign BusA = decoder_2_out4 ? register_4_q : 16'bz;  // Controlled_Buffer controlled_buffer_5
  assign BusA = decoder_2_out5 ? register_5_q : 16'bz;  // Controlled_Buffer controlled_buffer_6
  assign BusA = decoder_2_out6 ? register_6_q : 16'bz;  // Controlled_Buffer controlled_buffer_7
  assign BusA = decoder_2_out7 ? register_7_q : 16'bz;  // Controlled_Buffer controlled_buffer_8
  Decoder #(.enable("false"), .select(3)) decoder_3 (
    .out0(decoder_3_out0), .out1(decoder_3_out1), .out2(decoder_3_out2), .out3(decoder_3_out3),
    .out4(decoder_3_out4), .out5(decoder_3_out5), .out6(decoder_3_out6), .out7(decoder_3_out7), .sel(RB));
  assign BusB = decoder_3_out1 ? register_1_q : 16'bz;  // Controlled_Buffer controlled_buffer_9
  assign BusB = decoder_3_out2 ? register_2_q : 16'bz;  // Controlled_Buffer controlled_buffer_10
  assign BusB = decoder_3_out3 ? register_3_q : 16'bz;  // Controlled_Buffer controlled_buffer_11
  assign BusB = decoder_3_out4 ? register_4_q : 16'bz;  // Controlled_Buffer controlled_buffer_12
  assign BusB = decoder_3_out5 ? register_5_q : 16'bz;  // Controlled_Buffer controlled_buffer_13
  assign BusB = decoder_3_out6 ? register_6_q : 16'bz;  // Controlled_Buffer controlled_buffer_14
  assign BusB = decoder_3_out7 ? register_7_q : 16'bz;  // Controlled_Buffer controlled_buffer_15
  assign BusB = decoder_3_out0 ? {16{1'b0}} : 16'bz;  // Controlled_Buffer controlled_buffer_16
endmodule

module EX (
  input  RegW_in,
  input  [1:0] ALUSrc_in,
  input  MemRd_in,
  input  MemWr_in,
  input  WBData_in,
  input  JAL_in,
  input  LUI_in,
  input  [3:0] ALUOp_in,
  input  BEQ_in,
  input  BNE_in,
  input  clk,
  output RegW,
  output [1:0] ALUSrc,
  output MemRd,
  output MemWr,
  output WBData,
  output JAL,
  output LUI,
  output [3:0] ALUOp,
  output BEQ,
  output BNE
);

  Register #(.width(1)) register_1 (.D(RegW_in), .Q(RegW), .clk(clk));  // open: en, clr
  Register #(.width(2)) register_2 (.D(ALUSrc_in), .Q(ALUSrc), .clk(clk));  // open: en, clr
  Register #(.width(1)) register_3 (.D(MemRd_in), .Q(MemRd), .clk(clk));  // open: en, clr
  Register #(.width(1)) register_4 (.D(MemWr_in), .Q(MemWr), .clk(clk));  // open: en, clr
  Register #(.width(1)) register_5 (.D(WBData_in), .Q(WBData), .clk(clk));  // open: en, clr
  Register #(.width(1)) register_6 (.D(JAL_in), .Q(JAL), .clk(clk));  // open: en, clr
  Register #(.width(1)) register_7 (.D(LUI_in), .Q(LUI), .clk(clk));  // open: en, clr
  Register #(.width(4)) register_8 (.D(ALUOp_in), .Q(ALUOp), .clk(clk));  // open: en, clr
  Register #(.width(1)) register_9 (.D(BEQ_in), .Q(BEQ), .clk(clk));  // open: en, clr
  Register #(.width(1)) register_10 (.D(BNE_in), .Q(BNE), .clk(clk));  // open: en, clr
endmodule

module MEM (
  input  RegW_in,
  input  MemRd_in,
  input  MemWr_in,
  input  WBData_in,
  input  JAL_in,
  input  LUI_in,
  input  clk,
  output RegW,
  output MemRd,
  output MemWr,
  output WBData,
  output JAL,
  output LUI
);

  Register #(.width(1)) register_1 (.D(RegW_in), .Q(RegW), .clk(clk));  // open: en, clr
  Register #(.width(1)) register_2 (.D(MemRd_in), .Q(MemRd), .clk(clk));  // open: en, clr
  Register #(.width(1)) register_3 (.D(MemWr_in), .Q(MemWr), .clk(clk));  // open: en, clr
  Register #(.width(1)) register_4 (.D(WBData_in), .Q(WBData), .clk(clk));  // open: en, clr
  Register #(.width(1)) register_5 (.D(JAL_in), .Q(JAL), .clk(clk));  // open: en, clr
  Register #(.width(1)) register_6 (.D(LUI_in), .Q(LUI), .clk(clk));  // open: en, clr
endmodule

module WB (
  input  RegW_in,
  input  JAL_in,
  input  LUI_in,
  input  clk,
  output RegW,
  output JAL,
  output LUI
);

  Register #(.width(1)) register_1 (.D(RegW_in), .Q(RegW), .clk(clk));  // open: en, clr
  Register #(.width(1)) register_2 (.D(JAL_in), .Q(JAL), .clk(clk));  // open: en, clr
  Register #(.width(1)) register_3 (.D(LUI_in), .Q(LUI), .clk(clk));  // open: en, clr
endmodule

module PC_Ctrl2 (
  input  BEQ,
  input  BNE,
  input  J,
  input  Zero,
  output [1:0] PCSrc
);

  wire and_1_out, and_2_out, not_1_out, not_2_out;

  not not_1 (not_1_out, J);
  not not_2 (not_2_out, Zero);
  and and_1 (and_1_out, BNE, not_1_out, not_2_out);
  and and_2 (and_2_out, BEQ, not_1_out, Zero);
  or or_1 (PCSrc[1], and_1_out, and_2_out);

  assign PCSrc[0] = J;
endmodule

module Hazard_Detect_And_Forward (
  input  [2:0] Rs,
  input  [2:0] Rd2,
  input  Ex_RegWr,
  input  [2:0] Rd3,
  input  Mem_RegWr,
  input  [2:0] Rd4,
  input  WB_RegWr,
  input  EX_MemRd,
  input  [2:0] Rt,
  output [1:0] ForwardA,
  output Stall,
  output [1:0] ForwardB
);

  wire and_1_out, and_2_out, and_3_out, comparator_1_eq, comparator_2_eq, comparator_3_eq, comparator_4_eq,
       comparator_5_eq, comparator_6_eq, comparator_7_eq, comparator_8_eq, comparator_9_eq, comparator_10_eq,
       Cond1_out, Cond2_out, Cond3_out, or_5_out;

  Comparator #(.width(3)) comparator_1 (.a(3'b000), .b(Rs), .eq(comparator_1_eq));  // open: gt, lt
  Comparator #(.width(3)) comparator_2 (.a(Rs), .b(Rd2), .eq(comparator_2_eq));  // open: gt, lt
  Comparator #(.width(3)) comparator_3 (.a(Rs), .b(Rd3), .eq(comparator_3_eq));  // open: gt, lt
  Comparator #(.width(3)) comparator_4 (.a(Rs), .b(Rd4), .eq(comparator_4_eq));  // open: gt, lt
  Comparator #(.width(3)) comparator_5 (.a(3'b000), .b(Rt), .eq(comparator_5_eq));  // open: gt, lt
  Comparator #(.width(3)) comparator_6 (.a(Rt), .b(Rd2), .eq(comparator_6_eq));  // open: gt, lt
  Comparator #(.width(3)) comparator_7 (.a(Rt), .b(Rd3), .eq(comparator_7_eq));  // open: gt, lt
  Comparator #(.width(3)) comparator_8 (.a(Rt), .b(Rd4), .eq(comparator_8_eq));  // open: gt, lt
  and Cond1 (Cond1_out, ~comparator_1_eq, comparator_2_eq, Ex_RegWr);  // AND_Gate
  and and_1 (and_1_out, ~comparator_5_eq, comparator_6_eq, Ex_RegWr);  // AND_Gate
  and Cond2 (Cond2_out, ~Cond1_out, ~comparator_1_eq, comparator_3_eq, Mem_RegWr);  // AND_Gate
  and and_2 (and_2_out, ~and_1_out, ~comparator_5_eq, comparator_7_eq, Mem_RegWr);  // AND_Gate
  and Cond3 (Cond3_out, ~Cond1_out, ~Cond2_out, ~comparator_1_eq, comparator_4_eq, WB_RegWr);  // AND_Gate
  and and_3 (and_3_out, ~and_1_out, ~and_2_out, ~comparator_5_eq, comparator_8_eq, WB_RegWr);  // AND_Gate
  or or_1 (ForwardA[0], Cond1_out, Cond3_out);
  or or_2 (ForwardA[1], Cond2_out, Cond3_out);
  or or_3 (ForwardB[0], and_1_out, and_3_out);
  or or_4 (ForwardB[1], and_2_out, and_3_out);
  Comparator #(.mode("unsigned"), .width(2)) comparator_9 (
    .a(ForwardA), .b(2'b01), .eq(comparator_9_eq));  // open: gt, lt
  Comparator #(.mode("unsigned"), .width(2)) comparator_10 (
    .a(2'b01), .b(ForwardB), .eq(comparator_10_eq));  // open: gt, lt
  or or_5 (or_5_out, comparator_9_eq, comparator_10_eq);
  and and_4 (Stall, or_5_out, EX_MemRd);
endmodule

module StallMUX (
  input  Stall,
  input  RegWrite,
  input  MemRead,
  input  MemWrite,
  input  WBData,
  input  JAL,
  input  LUI,
  input  [1:0] ALUSrc,
  input  BEQ,
  input  BNE,
  input  [3:0] ALUOp,
  output RegWrite_out,
  output MemRead_out,
  output MemWrite_out,
  output WBData_out,
  output JAL_out,
  output LUI_out,
  output [1:0] ALUSrc_out,
  output BEQ_out,
  output BNE_out,
  output [3:0] ALUOp_out
);

  Multiplexer #(.width(14)) multiplexer_1 (
    .in0({ALUOp, BNE, BEQ, ALUSrc, LUI, JAL, WBData, MemWrite, MemRead, RegWrite}), .in1({14{1'b0}}),
    .out({ALUOp_out, BNE_out, BEQ_out, ALUSrc_out, LUI_out, JAL_out, WBData_out, MemWrite_out, MemRead_out, RegWrite_out}),
    .sel(Stall));
endmodule

module JALpipeline (
);

  wire [7:0] register_1_q, register_2_q, register_3_q, register_4_q, undriven;

  Register register_1 (.D(undriven), .Q(register_1_q));  // open: en, clk, clr
  Register register_2 (.D(register_1_q), .Q(register_2_q));  // open: en, clk, clr
  Register register_3 (.D(register_2_q), .Q(register_3_q));  // open: en, clk, clr
  Register register_4 (.D(register_3_q), .Q(register_4_q));  // open: en, clk, clr
endmodule

module PC_ctrl_jr (
  input  Jr,
  input  J,
  input  BNE,
  input  BEQ,
  input  Zero,
  output [1:0] PCSrc,
  output Kill1,
  output Kill2
);

  wire and_1_out, and_2_out, and_3_out, and_4_out;

  and and_1 (and_1_out, ~Zero, BNE);  // AND_Gate
  and and_2 (and_2_out, Zero, BEQ);
  or or_1 (Kill2, and_1_out, and_2_out);
  and and_3 (and_3_out, Jr, ~Kill2);  // AND_Gate
  and and_4 (and_4_out, J, ~Kill2);  // AND_Gate
  or Jr_Br (PCSrc[1], and_3_out, Kill2);
  or Kill (Kill1, and_4_out, and_3_out, Kill2);
  or J_Jr (PCSrc[0], and_3_out, and_4_out);
endmodule

module CU_Pipe3 (
  input  [4:0] OP,
  output [1:0] RegDst,
  output EXTOp,
  output RegWrite,
  output MemRead,
  output MemWrite,
  output WBData,
  output JAL,
  output LUI,
  output [1:0] ALUSrc,
  output BEQ,
  output BNE,
  output J,
  output Jr
);

  wire and_1_out, and_2_out, and_3_out, and_4_out, and_10_out, and_11_out, not_1_out, not_3_out, not_4_out,
       not_5_out;

  not not_1 (not_1_out, OP[4]);
  not not_2 (RegDst[0], OP[3]);
  not not_3 (not_3_out, OP[2]);
  not not_4 (not_4_out, OP[1]);
  not not_5 (not_5_out, OP[0]);
  and and_1 (and_1_out, not_4_out, not_5_out);
  and and_2 (and_2_out, not_1_out, not_3_out);
  and and_3 (and_3_out, not_1_out, not_4_out, not_5_out);
  and and_4 (and_4_out, OP[4], OP[0]);
  and and_5 (MemRead, OP[2], not_4_out, not_5_out);
  and and_6 (MemWrite, OP[2], not_4_out, OP[0]);
  and and_7 (WBData, OP[2], not_4_out);
  and and_8 (JAL, OP[4], RegDst[0], OP[0]);
  and and_9 (LUI, OP[4], OP[1]);
  and and_10 (and_10_out, OP[3], not_3_out);
  and and_11 (and_11_out, OP[2], not_4_out);
  and and_12 (BEQ, not_1_out, OP[3], OP[2], OP[1], not_5_out);
  and and_13 (BNE, not_1_out, OP[3], OP[2], OP[1], OP[0]);
  and and_14 (J, OP[4], RegDst[0], not_3_out, not_4_out, not_5_out);
  and and_15 (Jr, not_1_out, RegDst[0], not_3_out, OP[1], OP[0]);
  or or_1 (EXTOp, and_1_out, OP[2]);
  or or_2 (RegWrite, and_2_out, and_3_out, and_4_out);
  or or_3 (ALUSrc[0], and_10_out, and_11_out);

  assign ALUSrc[1] = OP[4];
  assign RegDst[1] = OP[4];
endmodule

module RevCtrl2 (
  input  [4:0] OP,
  input  [1:0] func,
  output x
);

  wire and_1_out, and_2_out, not_1_out, not_2_out, not_3_out, not_4_out, not_5_out;

  not not_1 (not_1_out, OP[4]);
  not not_2 (not_2_out, OP[3]);
  not not_3 (not_3_out, OP[2]);
  not not_4 (not_4_out, func[1]);
  not not_5 (not_5_out, func[0]);
  and and_1 (and_1_out, not_1_out, not_2_out, not_3_out, OP[1], OP[0], not_4_out);
  and and_2 (and_2_out, not_1_out, not_2_out, not_3_out, OP[1], OP[0], not_5_out);
  or or_1 (x, and_1_out, and_2_out);
endmodule

module CU_Pipe4 (
  input  [4:0] OP,
  output [1:0] RegDst,
  output EXTOp,
  output RegWrite,
  output MemRead,
  output MemWrite,
  output WBData,
  output JAL,
  output LUI,
  output [1:0] ALUSrc,
  output BEQ,
  output BNE,
  output J,
  output Jr
);

  wire and_1_out, and_2_out, and_3_out, and_4_out, and_10_out, and_11_out, not_1_out, not_3_out, not_4_out,
       not_5_out;

  not not_1 (not_1_out, OP[4]);
  not not_2 (RegDst[0], OP[3]);
  not not_3 (not_3_out, OP[2]);
  not not_4 (not_4_out, OP[1]);
  not not_5 (not_5_out, OP[0]);
  and and_1 (and_1_out, not_4_out, not_5_out);
  and and_2 (and_2_out, not_1_out, not_3_out);
  and and_3 (and_3_out, not_1_out, not_4_out, not_5_out);
  and and_4 (and_4_out, OP[4], OP[0]);
  and and_5 (MemRead, OP[2], not_4_out, not_5_out);
  and and_6 (MemWrite, OP[2], not_4_out, OP[0]);
  and and_7 (WBData, OP[2], not_4_out);
  and and_8 (JAL, OP[4], RegDst[0], OP[0]);
  and and_9 (LUI, OP[4], OP[1]);
  and and_10 (and_10_out, OP[3], not_3_out);
  and and_11 (and_11_out, OP[2], not_4_out);
  and and_12 (BEQ, not_1_out, OP[3], OP[2], OP[1], not_5_out);
  and and_13 (BNE, not_1_out, OP[3], OP[2], OP[1], OP[0]);
  and and_14 (J, OP[4], RegDst[0], not_3_out, not_4_out);
  and and_15 (Jr, not_1_out, RegDst[0], not_3_out, OP[1], OP[0]);
  or or_1 (EXTOp, and_1_out, OP[2]);
  or or_2 (RegWrite, and_2_out, and_3_out, and_4_out);
  or or_3 (ALUSrc[0], and_10_out, and_11_out);

  assign ALUSrc[1] = OP[4];
  assign RegDst[1] = OP[4];
endmodule
