// Logisim project SplitMain.circ as structural Verilog: 1 circuit, main circuit Splt
module Splt (
  input  [15:0] Inst16,
  output [10:0] Imm11,
  output [4:0] Op,
  output [2:0] Rt,
  output [2:0] Rs,
  output [4:0] Imm5,
  output [2:0] Rd,
  output [1:0] f2
);


  assign f2 = Inst16[10:9];
  assign Imm5 = Inst16[10:6];
  assign Imm11 = Inst16[10:0];
  assign Op = Inst16[15:11];
  assign Rd = Inst16[8:6];
  assign Rs = Inst16[5:3];
  assign Rt = Inst16[2:0];
endmodule
