// Logisim project arithmeticUnit.circ as structural Verilog: 1 circuit, main circuit arithmeticUnit
module arithmeticUnit (
  input  [15:0] A,
  input  [15:0] B,
  input  [1:0] SelectAR,
  output [15:0] OutputAR
);

  wire comparator_1_lt, comparator_2_lt;
  wire [15:0] adder_1_out, bit_extender_1_out, bit_extender_2_out, subtractor_1_out;

  Adder #(.width(16)) adder_1 (.a(A), .b(B), .out(adder_1_out));  // open: cin, cout
  Subtractor #(.width(16)) subtractor_1 (.a(A), .b(B), .out(subtractor_1_out));  // open: bin, bout
  Comparator #(.width(16)) comparator_1 (.a(A), .b(A), .lt(comparator_1_lt));  // open: gt, eq
  assign bit_extender_1_out = {{15{comparator_1_lt}}, comparator_1_lt};  // Bit_Extender bit_extender_1
  Comparator #(.mode("unsigned"), .width(16)) comparator_2 (.a(A), .b(A), .lt(comparator_2_lt));  // open: gt, eq
  assign bit_extender_2_out = {{15{comparator_2_lt}}, comparator_2_lt};  // Bit_Extender bit_extender_2
  Multiplexer #(.select(2), .width(16)) multiplexer_1 (
    .in0(adder_1_out), .in1(subtractor_1_out), .in2(bit_extender_1_out), .in3(bit_extender_2_out),
    .out(OutputAR), .sel(SelectAR));
endmodule
