// Logisim project logicUnit.circ as structural Verilog: 1 circuit, main circuit logicUnit
module logicUnit (
  input  [15:0] A,
  input  [15:0] B,
  input  [1:0] SelectLogic,
  output [15:0] OutputLogic
);

  wire [15:0] and_1_out, not_1_out, or_1_out, xor_1_out;

  assign and_1_out = A & B;  // AND_Gate and_1, 16 bits wide
  assign or_1_out = A | B;  // OR_Gate or_1, 16 bits wide
  assign xor_1_out = A ^ B;  // XOR_Gate xor_1, 16 bits wide
  assign not_1_out = ~or_1_out;  // NOT_Gate not_1, 16 bits wide
  Multiplexer #(.select(2), .width(16)) multiplexer_1 (
    .in0(and_1_out), .in1(or_1_out), .in2(xor_1_out), .in3(not_1_out), .out(OutputLogic), .sel(SelectLogic));
endmodule
