// Logisim project pcCounter.circ as structural Verilog: 1 circuit, main circuit thepc
module thepc (
  input  in_1,
  input  in_2,
  output [15:0] out_3
);

  wire clock_1_out;
  wire [15:0] adder_1_out;

  Register #(.width(16)) register_1 (.D(adder_1_out), .en(in_1), .Q(out_3), .clk(clock_1_out), .clr(in_2));
  Clock clock_1 (.out(clock_1_out));
  Adder #(.width(16)) adder_1 (.a(16'h1), .b(out_3), .out(adder_1_out));  // open: cin, cout
endmodule
