// Logisim project pipl.circ as structural Verilog: 12 circuits, main circuit pip
module pip (
);

  wire BEQ, BNE, clock_1_out, cu_pipe_1_beq, cu_pipe_1_bne, cu_pipe_1_jal, cu_pipe_1_lui, cu_pipe_1_memread,
       cu_pipe_1_memwrite, cu_pipe_1_regwrite, cu_pipe_1_wbdata, ex_1_jal, ex_1_lui, ex_1_memrd, ex_1_memwr,
       ex_1_regw, ex_1_wbdata, EXTOp, J, JAL, LUI, mem_1_jal, mem_1_lui, mem_1_regw, MemRead, MemWrite,
       not_1_out, not_2_out, RegWrite, REV_Src1, WBData, ZeroFlag;
  wire [1:0] ALUSrc, cu_pipe_1_alusrc, func, pc_ctrl2_1_p2, RegDst;
  wire [2:0] multiplexer_2_out, multiplexer_3_out, Rd2_q, Rd3_q, Rw, splt_1_rd, splt_1_rs, splt_1_rt;
  wire [3:0] ALUOp_1, aluop_1_aluop;
  wire [4:0] OP, splt_1_imm5;
  wire [10:0] splt_1_imm11;
  wire [15:0] A_q, adder_1_out, adder_2_out, alu_1_aluoutput, B_q, bit_extender_1_out, bit_extender_2_out,
       BTA_q, D_q, Data_q, Imm_q, Inst_q, multiplexer_1_out, multiplexer_4_out, multiplexer_5_out,
       multiplexer_6_out, multiplexer_7_out, NPC_q, R_q, ram_1_dout, register_1_q, registerfilee_1_busa,
       registerfilee_1_busb, rom_1_data;

  // PC_Ctrl2 pc_ctrl2_1: pin names not known; wires that end beside it: BEQ, pc_ctrl2_1_p2, BNE, J, ZeroFlag
  Multiplexer #(.select(2), .width(16)) multiplexer_1 (
    .in0(adder_1_out), .in1(bit_extender_1_out), .in2(BTA_q), .in3(A_q), .out(multiplexer_1_out),
    .sel(pc_ctrl2_1_p2));
  Adder #(.width(16)) adder_1 (.a(16'h1), .b(register_1_q), .out(adder_1_out));  // open: cin, cout
  Register #(.width(16)) register_1 (.D(multiplexer_1_out), .Q(register_1_q), .clk(clock_1_out));  // open: en, clr
  Clock clock_1 (.out(clock_1_out));
  ROM #(.addrWidth(16), .dataWidth(16)) rom_1 (.addr(register_1_q), .data(rom_1_data));
  Register #(.width(16)) NPC (.D(register_1_q), .Q(NPC_q), .clk(clock_1_out));  // open: en, clr
  Splt splt_1 (
    .Inst16(Inst_q), .Imm11(splt_1_imm11), .Op(OP), .Imm5(splt_1_imm5), .Rt(splt_1_rt), .Rs(splt_1_rs),
    .Rd(splt_1_rd), .f2(func));
  Register #(.width(16)) Inst (.D(rom_1_data), .Q(Inst_q), .clk(clock_1_out));  // open: en, clr
  Multiplexer #(.select(2), .width(3)) multiplexer_2 (
    .in0(splt_1_rt), .in1(splt_1_rd), .in2(3'b001), .in3(3'b111), .out(multiplexer_2_out), .sel(RegDst));
  Multiplexer #(.width(3)) multiplexer_3 (.in0(splt_1_rt), .in1(splt_1_rd), .out(multiplexer_3_out), .sel(REV_Src1));
  Adder #(.width(16)) adder_2 (.a(NPC_q), .b(Imm_q), .out(adder_2_out));  // open: cin, cout
  assign bit_extender_1_out = {{5{1'b0}}, splt_1_imm11};  // Bit_Extender bit_extender_1
  assign bit_extender_2_out = {{11{splt_1_imm5[4]}}, splt_1_imm5};  // Bit_Extender bit_extender_2
  registerFilee registerfilee_1 (
    .RW(Rw), .RegW(RegWrite), .BusW(multiplexer_4_out), .RA(splt_1_rs), .RB(multiplexer_3_out),
    .BusA(registerfilee_1_busa), .BusB(registerfilee_1_busb));
  Multiplexer #(.width(16)) multiplexer_4 (.in0(adder_1_out), .in1(Data_q), .out(multiplexer_4_out), .sel(not_1_out));
  not not_1 (not_1_out, JAL);
  CU_Pipe cu_pipe_1 (
    .OP(OP), .RegDst(RegDst), .RegWrite(cu_pipe_1_regwrite), .EXTOp(EXTOp), .ALUSrc(cu_pipe_1_alusrc),
    .MemRead(cu_pipe_1_memread), .MemWrite(cu_pipe_1_memwrite), .WBData(cu_pipe_1_wbdata),
    .JAL(cu_pipe_1_jal), .LUI(cu_pipe_1_lui), .BEQ(cu_pipe_1_beq), .BNE(cu_pipe_1_bne), .J(J));
  ALUOp u_aluop_1 (.OP(OP), .FUNC(func), .ALUOp(aluop_1_aluop));
  REV_SRC rev_src_1 (.OP(OP), .func(func), .out_3(REV_Src1));
  Register #(.width(16)) BTA (.D(adder_2_out), .Q(BTA_q));  // open: en, clk, clr
  Register #(.width(16)) Imm (.D(bit_extender_2_out), .Q(Imm_q));  // open: en, clk, clr
  Register #(.width(16)) A (.D(registerfilee_1_busa), .Q(A_q));  // open: en, clk, clr
  Register #(.width(16)) B (.D(registerfilee_1_busb), .Q(B_q));  // open: en, clk, clr
  Register #(.width(3)) Rd2 (.D(multiplexer_2_out), .Q(Rd2_q));  // open: en, clk, clr
  not not_2 (not_2_out, LUI);
  EX ex_1 (
    .RegW_in(cu_pipe_1_regwrite), .ALUSrc_in(cu_pipe_1_alusrc), .MemRd_in(cu_pipe_1_memread),
    .MemWr_in(cu_pipe_1_memwrite), .WBData_in(cu_pipe_1_wbdata), .JAL_in(cu_pipe_1_jal),
    .LUI_in(cu_pipe_1_lui), .ALUOp_in(aluop_1_aluop), .BEQ_in(cu_pipe_1_beq), .BNE_in(cu_pipe_1_bne),
    .RegW(ex_1_regw), .ALUSrc(ALUSrc), .MemRd(ex_1_memrd), .MemWr(ex_1_memwr), .WBData(ex_1_wbdata),
    .JAL(ex_1_jal), .LUI(ex_1_lui), .ALUOp(ALUOp_1), .BEQ(BEQ), .BNE(BNE));
  Multiplexer #(.width(16)) multiplexer_5 (
    .in0(bit_extender_1_out), .in1(A_q), .out(multiplexer_5_out), .sel(not_2_out));
  Multiplexer #(.select(2), .width(16)) multiplexer_6 (
    .in0(B_q), .in1(Imm_q), .in2(16'h5), .out(multiplexer_6_out), .sel(ALUSrc));  // open: in3
  ALU alu_1 (
    .ALUOp(ALUOp_1), .A(multiplexer_5_out), .B(multiplexer_6_out), .ALUOutput(alu_1_aluoutput),
    .ZeroFlag(ZeroFlag));
  Register #(.width(16)) R (.D(alu_1_aluoutput), .Q(R_q));  // open: en, clk, clr
  Register #(.width(16)) D (.D(B_q), .Q(D_q));  // open: en, clk, clr
  Register #(.width(3)) Rd3 (.D(Rd2_q), .Q(Rd3_q));  // open: en, clk, clr
  MEM mem_1 (
    .RegW_in(ex_1_regw), .MemRd_in(ex_1_memrd), .MemWr_in(ex_1_memwr), .WBData_in(ex_1_wbdata),
    .JAL_in(ex_1_jal), .LUI_in(ex_1_lui), .RegW(mem_1_regw), .MemRd(MemWrite), .MemWr(MemRead),
    .WBData(WBData), .JAL(mem_1_jal), .LUI(mem_1_lui));
  RAM #(.addrWidth(16), .asyncread("true"), .dataWidth(16)) ram_1 (
    .addr(R_q), .we(MemWrite), .oe(MemRead), .clk(clock_1_out), .din(D_q), .dout(ram_1_dout));
  Multiplexer #(.width(16)) multiplexer_7 (.in0(R_q), .in1(ram_1_dout), .out(multiplexer_7_out), .sel(WBData));
  Register #(.width(16)) Data (.D(multiplexer_7_out), .Q(Data_q));  // open: en, clk, clr
  Register #(.width(3)) Rd4 (.D(Rd3_q), .Q(Rw));  // open: en, clk, clr
  WB wb_1 (.RegW_in(mem_1_regw), .JAL_in(mem_1_jal), .LUI_in(mem_1_lui), .RegW(RegWrite), .JAL(JAL), .LUI(LUI));

  // Notes on the sheet:
  //   contents of rom_1 (hex, n*v repeats v):
  //   4141 a88 51c3 d1a 95c f84 495f 4a 28b 4f2 732 5955 104a 12f2 1532 175a ff6c 1c88 1a50 1888 4182 6914
  //   6115 68d5 168 cc9 7918 47db 70eb 4001 7959 77a5 0 0 0 8030 7009 11*0 4283 4004 40c5 6815 4064 4052
  //   7f63 4001 883a 8024 0 c92 4243 4006 680e 4049 4076 680e 67cc 600d 1ac 4049 4052 7e93 1e38
endmodule

module REV_SRC (
  input  [4:0] OP,
  input  [1:0] func,
  output out_3
);

  wire not_1_out, not_2_out, not_3_out, not_4_out;

  not not_1 (not_1_out, OP[4]);
  not not_2 (not_2_out, OP[3]);
  not not_3 (not_3_out, OP[2]);
  not not_4 (not_4_out, func[1]);
  and and_1 (out_3, not_1_out, not_2_out, not_3_out, OP[1], OP[0], not_4_out);
endmodule

module PC_Ctrl (
  input  [4:0] OP,
  input  [1:0] FUNC,
  input  Zero,
  output [1:0] PCSrc
);

  wire and_1_out, and_2_out, not_1_out, not_2_out, not_3_out, not_4_out, not_5_out, not_6_out;

  not not_1 (not_1_out, OP[4]);
  not not_2 (not_2_out, OP[3]);
  not not_3 (not_3_out, OP[2]);
  not not_4 (not_4_out, OP[1]);
  not not_5 (not_5_out, OP[0]);
  not not_6 (not_6_out, Zero);
  and and_1 (and_1_out, not_1_out, OP[3], OP[2], OP[1], not_5_out, Zero);
  and and_2 (and_2_out, not_1_out, OP[3], OP[2], OP[1], OP[0], not_6_out);
  and and_3 (PCSrc[0], OP[4], not_2_out, not_3_out, not_4_out);
  or or_1 (PCSrc[1], and_1_out, and_2_out);
endmodule

module ALUOp (
  input  [4:0] OP,
  input  [1:0] FUNC,
  output [3:0] ALUOp
);

  wire and_1_out, and_2_out, and_3_out, and_4_out, and_5_out, and_6_out, and_7_out, and_8_out, and_9_out,
       and_10_out, and_11_out, not_1_out, not_2_out, not_3_out, not_4_out, not_5_out;

  not not_1 (not_1_out, OP[4]);
  not not_2 (not_2_out, OP[3]);
  not not_3 (not_3_out, OP[2]);
  not not_4 (not_4_out, OP[1]);
  not not_5 (not_5_out, OP[0]);
  and and_1 (and_1_out, not_3_out, OP[0]);
  and and_2 (and_2_out, OP[3], not_3_out, OP[1]);
  and and_3 (and_3_out, not_2_out, OP[1], OP[0]);
  and and_4 (and_4_out, not_1_out, not_4_out, not_5_out);
  and and_5 (and_5_out, not_1_out, OP[3], OP[2]);
  and and_6 (and_6_out, not_2_out, not_4_out, not_5_out);
  and and_7 (and_7_out, not_2_out, FUNC[1]);
  and and_8 (and_8_out, OP[3], not_3_out, OP[1], OP[0]);
  and and_9 (and_9_out, not_2_out, FUNC[0]);
  and and_10 (and_10_out, OP[3], OP[1], not_5_out);
  and and_11 (and_11_out, not_1_out, OP[2], OP[1]);
  or or_1 (ALUOp[3], and_1_out, and_2_out);
  or or_2 (ALUOp[2], and_3_out, and_4_out, and_5_out, and_6_out);
  or or_3 (ALUOp[1], and_7_out, and_8_out);
  or or_4 (ALUOp[0], and_9_out, and_10_out, and_11_out);
endmodule

module CU (
  input  [4:0] OP,
  output [1:0] RegDst,
  output RegWrite,
  output EXTOp,
  output [1:0] ALUSrc,
  output MemRead,
  output MemWrite,
  output WBData,
  output JAL,
  output LUI
);

  wire and_1_out, and_2_out, and_3_out, and_4_out, and_5_out, and_6_out, not_1_out, not_3_out, not_4_out,
       not_5_out;

  not not_1 (not_1_out, OP[4]);
  not not_2 (RegDst[0], OP[3]);
  not not_3 (not_3_out, OP[2]);
  not not_4 (not_4_out, OP[1]);
  not not_5 (not_5_out, OP[0]);
  and and_1 (and_1_out, not_1_out, not_3_out);
  and and_2 (and_2_out, not_1_out, not_4_out, not_5_out);
  and and_3 (and_3_out, OP[4], OP[0]);
  and and_4 (and_4_out, not_4_out, not_5_out);
  and and_5 (and_5_out, OP[3], not_3_out);
  and and_6 (and_6_out, OP[2], not_4_out);
  and and_7 (MemRead, OP[2], not_4_out, not_5_out);
  and and_8 (MemWrite, OP[2], not_4_out, OP[0]);
  and and_9 (WBData, OP[2], not_4_out);
  and and_10 (JAL, OP[4], RegDst[0], OP[0]);
  and and_11 (LUI, OP[4], OP[1]);
  or or_1 (RegWrite, and_1_out, and_2_out, and_3_out);
  or or_2 (EXTOp, and_4_out, OP[2]);
  or or_3 (ALUSrc[0], and_5_out, and_6_out);

  assign ALUSrc[1] = OP[4];
  assign RegDst[1] = OP[4];
endmodule

module Split (
  input  [15:0] Inst16,
  output [10:0] Imm11,
  output [4:0] Op,
  output [2:0] Rt,
  output [2:0] Rs,
  output [4:0] Imm5,
  output [2:0] Rd,
  output [1:0] f2
);


  assign f2 = Inst16[10:9];
  assign Imm5 = Inst16[10:6];
  assign Imm11 = Inst16[10:0];
  assign Op = Inst16[15:11];
  assign Rd = Inst16[8:6];
  assign Rs = Inst16[5:3];
  assign Rt = Inst16[2:0];
endmodule

module registerFilee (
  input  [2:0] RA,
  input  [2:0] RB,
  input  [15:0] BusW,
  input  [2:0] RW,
  input  RegW,
  output [15:0] BusB,
  output [15:0] BusA
);

  wire and_1_out, and_2_out, and_3_out, and_4_out, and_5_out, and_6_out, and_7_out, clock_1_out,
       decoder_1_out1, decoder_1_out2, decoder_1_out3, decoder_1_out4, decoder_1_out5, decoder_1_out6,
       decoder_1_out7, decoder_2_out0, decoder_2_out1, decoder_2_out2, decoder_2_out3, decoder_2_out4,
       decoder_2_out5, decoder_2_out6, decoder_2_out7, decoder_3_out0, decoder_3_out1, decoder_3_out2,
       decoder_3_out3, decoder_3_out4, decoder_3_out5, decoder_3_out6, decoder_3_out7;
  wire [15:0] register_1_q, register_2_q, register_3_q, register_4_q, register_5_q, register_6_q,
       register_7_q;

  Decoder #(.enable("false"), .select(3)) decoder_1 (
    .out1(decoder_1_out1), .out2(decoder_1_out2), .out3(decoder_1_out3), .out4(decoder_1_out4),
    .out5(decoder_1_out5), .out6(decoder_1_out6), .out7(decoder_1_out7), .sel(RW));  // open: out0
  and and_1 (and_1_out, decoder_1_out1, RegW);
  and and_2 (and_2_out, decoder_1_out2, RegW);
  and and_3 (and_3_out, decoder_1_out3, RegW);
  and and_4 (and_4_out, decoder_1_out4, RegW);
  and and_5 (and_5_out, decoder_1_out5, RegW);
  and and_6 (and_6_out, decoder_1_out6, RegW);
  and and_7 (and_7_out, decoder_1_out7, RegW);
  Decoder #(.enable("false"), .select(3)) decoder_2 (
    .out0(decoder_2_out0), .out1(decoder_2_out1), .out2(decoder_2_out2), .out3(decoder_2_out3),
    .out4(decoder_2_out4), .out5(decoder_2_out5), .out6(decoder_2_out6), .out7(decoder_2_out7), .sel(RA));
  Register #(.width(16)) register_1 (.D(BusW), .en(and_1_out), .Q(register_1_q), .clk(clock_1_out));  // open: clr
  Register #(.width(16)) register_2 (.D(BusW), .en(and_2_out), .Q(register_2_q), .clk(clock_1_out));  // open: clr
  Register #(.width(16)) register_3 (.D(BusW), .en(and_3_out), .Q(register_3_q), .clk(clock_1_out));  // open: clr
  Register #(.width(16)) register_4 (.D(BusW), .en(and_4_out), .Q(register_4_q), .clk(clock_1_out));  // open: clr
  Register #(.width(16)) register_5 (.D(BusW), .en(and_5_out), .Q(register_5_q), .clk(clock_1_out));  // open: clr
  Register #(.width(16)) register_6 (.D(BusW), .en(and_6_out), .Q(register_6_q), .clk(clock_1_out));  // open: clr
  Register #(.width(16)) register_7 (.D(BusW), .en(and_7_out), .Q(register_7_q), .clk(clock_1_out));  // open: clr
  Clock clock_1 (.out(clock_1_out));
  assign BusA = decoder_2_out0 ? {16{1'b0}} : 16'bz;  // Controlled_Buffer controlled_buffer_1
  assign BusA = decoder_2_out1 ? register_1_q : 16'bz;  // Controlled_Buffer controlled_buffer_2
  assign BusA = decoder_2_out2 ? register_2_q : 16'bz;  // Controlled_Buffer controlled_buffer_3
  assign BusA = decoder_2_out3 ? register_3_q : 16'bz;  // Controlled_Buffer controlled_buffer_4
  assign BusA = decoder_2_out4 ? register_4_q : 16'bz;  // Controlled_Buffer controlled_buffer_5
  assign BusA = decoder_2_out5 ? register_5_q : 16'bz;  // Controlled_Buffer controlled_buffer_6
  assign BusA = decoder_2_out6 ? register_6_q : 16'bz;  // Controlled_Buffer controlled_buffer_7
  assign BusA = decoder_2_out7 ? register_7_q : 16'bz;  // Controlled_Buffer controlled_buffer_8
  Decoder #(.enable("false"), .select(3)) decoder_3 (
    .out0(decoder_3_out0), .out1(decoder_3_out1), .out2(decoder_3_out2), .out3(decoder_3_out3),
    .out4(decoder_3_out4), .out5(decoder_3_out5), .out6(decoder_3_out6), .out7(decoder_3_out7), .sel(RB));
  assign BusB = decoder_3_out1 ? register_1_q : 16'bz;  // Controlled_Buffer controlled_buffer_9
  assign BusB = decoder_3_out2 ? register_2_q : 16'bz;  // Controlled_Buffer controlled_buffer_10
  assign BusB = decoder_3_out3 ? register_3_q : 16'bz;  // Controlled_Buffer controlled_buffer_11
  assign BusB = decoder_3_out4 ? register_4_q : 16'bz;  // Controlled_Buffer controlled_buffer_12
  assign BusB = decoder_3_out5 ? register_5_q : 16'bz;  // Controlled_Buffer controlled_buffer_13
  assign BusB = decoder_3_out6 ? register_6_q : 16'bz;  // Controlled_Buffer controlled_buffer_14
  assign BusB = decoder_3_out7 ? register_7_q : 16'bz;  // Controlled_Buffer controlled_buffer_15
  assign BusB = decoder_3_out0 ? {16{1'b0}} : 16'bz;  // Controlled_Buffer controlled_buffer_16
endmodule

module EX (
  input  RegW_in,
  input  [1:0] ALUSrc_in,
  input  MemRd_in,
  input  MemWr_in,
  input  WBData_in,
  input  JAL_in,
  input  LUI_in,
  input  [3:0] ALUOp_in,
  input  BEQ_in,
  input  BNE_in,
  output RegW,
  output [1:0] ALUSrc,
  output MemRd,
  output MemWr,
  output WBData,
  output JAL,
  output LUI,
  output [3:0] ALUOp,
  output BEQ,
  output BNE
);

  Register #(.width(1)) register_1 (.D(RegW_in), .Q(RegW));  // open: en, clk, clr
  Register #(.width(2)) register_2 (.D(ALUSrc_in), .Q(ALUSrc));  // open: en, clk, clr
  Register #(.width(1)) register_3 (.D(MemRd_in), .Q(MemRd));  // open: en, clk, clr
  Register #(.width(1)) register_4 (.D(MemWr_in), .Q(MemWr));  // open: en, clk, clr
  Register #(.width(1)) register_5 (.D(WBData_in), .Q(WBData));  // open: en, clk, clr
  Register #(.width(1)) register_6 (.D(JAL_in), .Q(JAL));  // open: en, clk, clr
  Register #(.width(1)) register_7 (.D(LUI_in), .Q(LUI));  // open: en, clk, clr
  Register #(.width(4)) register_8 (.D(ALUOp_in), .Q(ALUOp));  // open: en, clk, clr
  Register #(.width(1)) register_9 (.D(BEQ_in), .Q(BEQ));  // open: en, clk, clr
  Register #(.width(1)) register_10 (.D(BNE_in), .Q(BNE));  // open: en, clk, clr
endmodule

module MEM (
  input  RegW_in,
  input  MemRd_in,
  input  MemWr_in,
  input  WBData_in,
  input  JAL_in,
  input  LUI_in,
  output RegW,
  output MemRd,
  output MemWr,
  output WBData,
  output JAL,
  output LUI
);

  Register #(.width(1)) register_1 (.D(RegW_in), .Q(RegW));  // open: en, clk, clr
  Register #(.width(1)) register_2 (.D(MemRd_in), .Q(MemRd));  // open: en, clk, clr
  Register #(.width(1)) register_3 (.D(MemWr_in), .Q(MemWr));  // open: en, clk, clr
  Register #(.width(1)) register_4 (.D(WBData_in), .Q(WBData));  // open: en, clk, clr
  Register #(.width(1)) register_5 (.D(JAL_in), .Q(JAL));  // open: en, clk, clr
  Register #(.width(1)) register_6 (.D(LUI_in), .Q(LUI));  // open: en, clk, clr
endmodule

module WB (
  input  RegW_in,
  input  JAL_in,
  input  LUI_in,
  output RegW,
  output JAL,
  output LUI
);

  Register #(.width(1)) register_1 (.D(RegW_in), .Q(RegW));  // open: en, clk, clr
  Register #(.width(1)) register_2 (.D(JAL_in), .Q(JAL));  // open: en, clk, clr
  Register #(.width(1)) register_3 (.D(LUI_in), .Q(LUI));  // open: en, clk, clr
endmodule

module CU_Pipe (
  input  [4:0] OP,
  output [1:0] RegDst,
  output RegWrite,
  output EXTOp,
  output [1:0] ALUSrc,
  output MemRead,
  output MemWrite,
  output WBData,
  output JAL,
  output LUI,
  output BEQ,
  output BNE,
  output J
);

  wire and_1_out, and_2_out, and_3_out, and_4_out, and_5_out, and_6_out, not_1_out, not_3_out, not_4_out,
       not_5_out;

  not not_1 (not_1_out, OP[4]);
  not not_2 (RegDst[0], OP[3]);
  not not_3 (not_3_out, OP[2]);
  not not_4 (not_4_out, OP[1]);
  not not_5 (not_5_out, OP[0]);
  and and_1 (and_1_out, not_1_out, not_3_out);
  and and_2 (and_2_out, not_1_out, not_4_out, not_5_out);
  and and_3 (and_3_out, OP[4], OP[0]);
  and and_4 (and_4_out, not_4_out, not_5_out);
  and and_5 (and_5_out, OP[3], not_3_out);
  and and_6 (and_6_out, OP[2], not_4_out);
  and and_7 (MemRead, OP[2], not_4_out, not_5_out);
  and and_8 (MemWrite, OP[2], not_4_out, OP[0]);
  and and_9 (WBData, OP[2], not_4_out);
  and and_10 (JAL, OP[4], RegDst[0], OP[0]);
  and and_11 (LUI, OP[4], OP[1]);
  and and_12 (BEQ, not_1_out, OP[3], OP[2], OP[1], not_5_out);
  and and_13 (BNE, not_1_out, OP[3], OP[2], OP[1], OP[0]);
  and and_14 (J, OP[4], RegDst[0], not_3_out, not_4_out, not_5_out);
  or or_1 (RegWrite, and_1_out, and_2_out, and_3_out);
  or or_2 (EXTOp, and_4_out, OP[2]);
  or or_3 (ALUSrc[0], and_5_out, and_6_out);

  assign ALUSrc[1] = OP[4];
  assign RegDst[1] = OP[4];
endmodule

module PC_Ctrl2 (
  input  BEQ,
  input  BNE,
  input  J,
  input  Zero,
  output [1:0] PCSrc
);

  wire and_1_out, and_2_out, not_1_out, not_2_out;

  not not_1 (not_1_out, J);
  not not_2 (not_2_out, Zero);
  and and_1 (and_1_out, BNE, not_1_out, not_2_out);
  and and_2 (and_2_out, BEQ, not_1_out, Zero);
  or or_1 (PCSrc[1], and_1_out, and_2_out);

  assign PCSrc[0] = J;
endmodule
