// Logisim project reverseUnit.circ as structural Verilog: 1 circuit, main circuit reverse
module reverse (
  input  [15:0] A,
  input  [15:0] B,
  input  [1:0] SelectReverse,
  output [15:0] OutputReverse
);

  Multiplexer #(.select(2), .width(16)) multiplexer_1 (
    .in0({B[15:8], A[0], A[1], A[2], A[3], A[4], A[5], A[6], A[7]}),
    .in1({B[15:8], A[8], A[9], A[10], A[11], A[12], A[13], A[14], A[15]}),
    .in2({A[0], A[1], A[2], A[3], A[4], A[5], A[6], A[7], A[8], A[9], A[10], A[11], A[12], A[13], A[14], A[15]}),
    .out(OutputReverse), .sel(SelectReverse));  // open: in3
endmodule
