// Logisim project shiftUnit.circ as structural Verilog: 1 circuit, main circuit shiftUnit
module shiftUnit (
  input  [15:0] A,
  input  [15:0] B,
  input  [1:0] SelectShift,
  output [15:0] OutputShift
);

  wire [15:0] shifter_1_out, shifter_2_out, shifter_3_out, shifter_4_out;

  Shifter #(.width(16)) shifter_1 (.in(B), .\dist (A[3:0]), .out(shifter_1_out));
  Shifter #(.shift("lr"), .width(16)) shifter_2 (.in(B), .\dist (A[3:0]), .out(shifter_2_out));
  Shifter #(.shift("ar"), .width(16)) shifter_3 (.in(B), .\dist (A[3:0]), .out(shifter_3_out));
  Shifter #(.shift("rr"), .width(16)) shifter_4 (.in(B), .\dist (A[3:0]), .out(shifter_4_out));
  Multiplexer #(.select(2), .width(16)) multiplexer_1 (
    .in0(shifter_1_out), .in1(shifter_2_out), .in2(shifter_3_out), .in3(shifter_4_out), .out(OutputShift),
    .sel(SelectShift));
endmodule
